# Fritzing sketch Untitled Sketch 2 (saved by Fritzing 0.9.3b)
breadboards: 1

parts:
  Raspberry_Pi_1 = Raspberry Pi 3 [part_number=RPI-3-V1.2]
  J1 = Power Jack [package=power_jack_pth_lock]
  J5 = Basic Servo
  J4 = Basic Servo

nets:
  N1: Raspberry_Pi_1.GPIO17, J4.pulse
  N2: Raspberry_Pi_1.GPIO18, J5.pulse
  GND: J1.GND, J1.GNDBREAK, J5.gnd, J4.gnd
  N3: J1.PWR, J4.vcc
